# Fritzing sketch Kiste (saved by Fritzing 0.9.2b)
circuit board: 5cm x 5cm
breadboards: 1

parts:
  Nano = Arduino Nano (Rev3.0)
  LED2 = screw terminal, 6 pins
  Main = Screw terminal - 2 pins [package=THT]
  LED1 = screw terminal, 6 pins
  Touch = screw terminal, 8 pins
  R3 = Resistor [tolerance=±5% resistance=300 package=THT]
  R4 = Resistor [tolerance=±5% resistance=300 package=THT]
  R2 = Resistor [tolerance=±5% resistance=300 package=THT]
  R1 = Resistor [tolerance=±5% resistance=300 package=THT]

nets:
  N1: Nano.GND, LED2.pin2, LED2.pin5, Main.pin1, LED1.pin2, LED1.pin5, Touch.pin2
  N2: Nano.D3, R3.Pin_1
  N3: Nano.D4, R4.Pin_1
  N4: Nano.D5, R1.Pin_1
  N5: Nano.D6, R2.Pin_1
  N6: Nano.D7, Touch.pin3
  N7: Nano.D8, Touch.pin4
  N8: Nano.D9, Touch.pin5
  N9: Nano.D10, Touch.pin6
  N10: Nano.D11/MOSI, Touch.pin7
  N11: Nano.VIN, LED2.pin1, LED2.pin4, Main.pin2, LED1.pin1, LED1.pin4
  N12: Nano.5V, Touch.pin1
  N13: LED2.pin3, R3.Pin_0
  N14: LED2.pin6, R4.Pin_0
  N15: LED1.pin3, R1.Pin_0
  N16: LED1.pin6, R2.Pin_0

notes:
  + - 1 2 3 4 5
  + - 3 + - 4
  + - 1 + - 2
  findl.ING LC02
  Light controller
  NeoPixel and Touch
  +
  -
  http://findl.ing.gl
