# Fritzing sketch LightController2 (saved by Fritzing 0.9.2b)
circuit board: 5cm x 5cm
breadboards: 1

parts:
  Arduino_Nano = Arduino Nano (Rev3.0) [part_number=Arduino]
  Q1 = MOSFET-NCHANNEL [part_number=MOSFET1 package=to220v]
  R5 = Resistor [tolerance=±5% resistance=10k package=THT]
  R3 = Resistor [tolerance=±5% resistance=10k package=THT]
  R4 = Resistor [tolerance=±5% resistance=10k package=THT]
  J1 = Screw terminal - 2 pins [part_number=LED1 package=THT]
  J2 = Screw terminal - 2 pins [part_number=LDR1 package=THT]
  J3 = Screw terminal - 2 pins [part_number=LDR2 package=THT]
  J4 = Screw terminal - 2 pins [package=THT]

nets:
  N1: Arduino_Nano.GND, Q1.S, R5.Pin_1, R3.Pin_0, R4.Pin_0, J2.pin1, J3.pin1, J4.pin1
  N2: Arduino_Nano.D2, Q1.G, R5.Pin_0
  N3: Arduino_Nano.VIN, J1.pin2, J4.pin2
  N4: Arduino_Nano.5V, R3.Pin_1, R4.Pin_1
  N5: Arduino_Nano.A2, J2.pin2
  N6: Arduino_Nano.A1, J3.pin2
  N7: Q1.D, J1.pin1
