# Fritzing sketch LightControllerHallSensor1 (saved by Fritzing 0.9.2b)
circuit board: 5cm x 5cm
breadboards: 2

parts:
  findl_ing_gl_LC_1 = Arduino Nano (Rev3.0)
  MAIN = Screw terminal - 2 pins [package=THT]
  LDR1 = Screw terminal - 2 pins [package=THT]
  LDR2 = Screw terminal - 2 pins [package=THT]
  LDR3 = Screw terminal - 2 pins [package=THT]
  CAP4 = Screw terminal - 2 pins [part_number=CAP4 package=THT]
  CAP3 = Screw terminal - 2 pins [part_number=CAP3 package=THT]
  CAP2 = Screw terminal - 2 pins [part_number=CAP2 package=THT]
  LED1 = Screw terminal - 2 pins [package=THT]
  LED2 = Screw terminal - 2 pins [package=THT]
  LED3 = Screw terminal - 2 pins [package=THT]
  LED1_2 = Basic FET P-Channel [package="TO220 [THT]"]
  LED2_2 = Basic FET P-Channel [package="TO220 [THT]"]
  LED3_2 = Basic FET P-Channel [package="TO220 [THT]"]
  LED1_3 = Resistor [tolerance=±5% resistance=10k package=THT]
  LED2_3 = Resistor [tolerance=±5% resistance=10k package=THT]
  LED3_3 = Resistor [tolerance=±5% resistance=10k package=THT]
  C1 = Capacitor Polarized [package=cpol-radial-100uf-25v]
  C2 = Capacitor [package=cap-pth-small2]
  LDR1_2 = Resistor [tolerance=±5% resistance=10k package=THT]
  LDR2_2 = Resistor [tolerance=±5% resistance=10k package=THT]
  CAP1 = Screw terminal - 2 pins [part_number=CAP1 package=THT]
  LDR3_2 = Resistor [tolerance=±5% resistance=10k package=THT]
  HALL1 = Screw terminal - 2 pins [package=THT]
  HALL2 = Screw terminal - 2 pins [package=THT]
  HALL3 = Screw terminal - 2 pins [package=THT]
  HALL4 = Screw terminal - 2 pins [package=THT]
  HALL5 = Screw terminal - 2 pins [package=THT]
  HALL6 = Screw terminal - 2 pins [package=THT]
  HALL2_2 = Resistor [tolerance=±5% resistance=10k package=THT]
  HALL1_2 = Resistor [tolerance=±5% resistance=10k package=THT]
  HALL3_2 = Resistor [tolerance=±5% resistance=10k package=THT]
  HALL4_2 = Resistor [tolerance=±5% resistance=10k package=THT]

nets:
  N1: findl_ing_gl_LC_1.GND, MAIN.pin2, LDR1.pin2, LDR2.pin2, LDR3.pin2, LED1_2.source, LED2_2.source, LED3_2.source, LED1_3.Pin_1, LED2_3.Pin_1, LED3_3.Pin_1, C1.-, C2.2, CAP1.pin2, HALL1.pin2, HALL3.pin1, HALL4.pin2, HALL6.pin1
  N2: findl_ing_gl_LC_1.D3, LED1_2.gate, LED1_3.Pin_0
  N3: findl_ing_gl_LC_1.D5, LED3_2.gate, LED3_3.Pin_0
  N4: findl_ing_gl_LC_1.D6, LED2_2.gate, LED2_3.Pin_0
  N5: findl_ing_gl_LC_1.D8, CAP2.pin2
  N6: findl_ing_gl_LC_1.D9, CAP2.pin1
  N7: findl_ing_gl_LC_1.D10, CAP3.pin2
  N8: findl_ing_gl_LC_1.D11/MOSI, CAP3.pin1
  N9: findl_ing_gl_LC_1.D12/MISO, CAP4.pin2
  N10: findl_ing_gl_LC_1.VIN, MAIN.pin1, LED1.pin1, LED2.pin1, LED3.pin1, C1.+, C2.1
  N11: findl_ing_gl_LC_1.5V, LDR1_2.Pin_0, LDR2_2.Pin_0, CAP1.pin1, LDR3_2.Pin_0, HALL1.pin1, HALL2.pin2, HALL4.pin1, HALL5.pin2, HALL2_2.Pin_1, HALL1_2.Pin_1, HALL3_2.Pin_1, HALL4_2.Pin_1
  N12: findl_ing_gl_LC_1.A6, HALL2.pin1, HALL1_2.Pin_0
  N13: findl_ing_gl_LC_1.A5, HALL3.pin2, HALL2_2.Pin_0
  N14: findl_ing_gl_LC_1.A4, HALL5.pin1, HALL3_2.Pin_0
  N15: findl_ing_gl_LC_1.A3, HALL6.pin2, HALL4_2.Pin_0
  N16: findl_ing_gl_LC_1.A2, LDR3.pin1, LDR3_2.Pin_1
  N17: findl_ing_gl_LC_1.A1, LDR2.pin1, LDR2_2.Pin_1
  N18: findl_ing_gl_LC_1.A0, LDR1.pin1, LDR1_2.Pin_1
  N19: LED1.pin2, LED1_2.drain
  N20: LED2.pin2, LED2_2.drain
  N21: LED3.pin2, LED3_2.drain
