# Fritzing sketch LightControllerLDR1 (saved by Fritzing 0.9.2b)
circuit board: 5cm x 5cm
breadboards: 1

parts:
  J1 = Screw terminal - 2 pins [package=THT]
  C1 = Ceramic Capacitor [capacitance="100 nF" package="1206 [SMD, multilayer]"]
  J2 = screw terminal, 4 pins
  R1 = Resistor [tolerance=±5% resistance=10k package=THT]
  R2 = Resistor [tolerance=±5% resistance=10k package=THT]
  LED3 = Basic FET N-Channel [package="TO220 [THT]"]
  R3 = Resistor [tolerance=±5% resistance=10k package=THT]
  J4 = screw terminal, 6 pins
  R4 = Resistor [tolerance=±5% resistance=10k package=THT]
  LED2 = Basic FET N-Channel [package="TO220 [THT]"]
  R5 = Resistor [tolerance=±5% resistance=10k package=THT]
  LED1 = Basic FET N-Channel [package="TO220 [THT]"]
  C2 = Capacitor Polarized [package=cpol-radial-10uf-25v]
  J3 = screw terminal, 8 pins
  Nano = Arduino Nano v2.3

nets:
  N1: J1.pin1, C1.1, LED3.source, R3.Pin_1, R4.Pin_1, LED2.source, R5.Pin_1, LED1.source, C2.-, J3.pin8, Nano.GND
  N2: J1.pin2, C1.0, J4.pin1, J4.pin3, J4.pin5, C2.+, Nano.VIN
  N3: J2.pin1, Nano.A6
  N4: J2.pin2, R2.Pin_1
  N5: J2.pin3, Nano.A5
  N6: J2.pin4, R1.Pin_1
  N7: R1.Pin_0, R2.Pin_0, J3.pin7, Nano.+5V
  N8: LED3.gate, R3.Pin_0, Nano.D6
  N9: LED3.drain, J4.pin6
  N10: J4.pin2, LED1.drain
  N11: J4.pin4, LED2.drain
  N12: R4.Pin_0, LED2.gate, Nano.D5
  N13: R5.Pin_0, LED1.gate, Nano.D3
  N14: J3.pin2, Nano.A4
  N15: J3.pin3, Nano.A3
  N16: J3.pin4, Nano.A2
  N17: J3.pin5, Nano.A1
  N18: J3.pin6, Nano.A0

notes:
  -
  d
  g
  s
  +
  VDD
  Gnd
  0
  1
  2
  3
  4
  Kabel zu AT42QT1070
  Kabel zu LDR
  LDR2
  LDR1
  Kabel zu LED
  12V
  10k
  findl.ing.gl
  Designer: Matthias Schwitter
  Engineer: Nils Birkeland
  findl.ING - Mitdenkende Möbel
  LCLDRv1.0
