# Fritzing sketch Electronix (saved by Fritzing 0.9.0b)
breadboards: 1

parts:
  CAPTOUCH1 = CAP1188 8-Key Captouch
  Bauteil1 = Arduino Uno (Rev3) - ICSP
  U1 = 3.5mm Audio Jack [package=audio-jack-3.5mm-smd]  # not connected
  SPKR1 = Loudspeaker  # not connected
  Q1 = Basic FET N-Channel [package="DPak [SMD]"]
  R1 = Resistor [tolerance=±5% resistance=10k package="1206 [SMD]"]
  J1 = Power Jack [package=power_jack_smd]
  LED1 = LED - 3mm [color="White (8000K)" package="3 mm [THT]"]

nets:
  N1: CAPTOUCH1.SDA/MISO, Bauteil1.A4/SDA
  N2: CAPTOUCH1.SCK, Bauteil1.A5/SCL
  VIN: CAPTOUCH1.VIN, Bauteil1.5V
  GND: CAPTOUCH1.GND, Bauteil1.GND
  N3: Bauteil1.D6_PWM, Q1.Gate, R1.Pin_0
  N4: Q1.drain, LED1.anode
  N5: Q1.source, R1.Pin_1, J1.GND
  N6: J1.GNDBREAK, LED1.cathode

custom parts:
  CAP1188 8-Key Captouch: CAP1188 8-Key Captouch Breakout
