# Fritzing sketch FrontDoor (saved by Fritzing 0.8.3b)
breadboards: 1

parts:
  Power_plug1 = Power plug
  S3 = Round Pushbutton
  S4 = Round Pushbutton
  Bauteil1 = Arduino Uno (Rev3)
  U1 = Optocoupler [package=THT]
  U2 = Optocoupler [package=THT]
  R1 = Resistor [tolerance=±5% resistance=1k package=THT]
  R3 = Resistor [tolerance=±5% resistance=10k package=THT]
  R4 = Resistor [tolerance=±5% resistance=10k package=THT]
  LED1 = LEDs [package=led10mm]
  R2 = Resistor [tolerance=±5% resistance=1k package=THT]
  LED2 = LEDs [package=led10mm]

nets:
  GND: Power_plug1.GND, Bauteil1.GND, LED1.C, LED2.C
  VCC: Power_plug1.VCC, S3.leg0, S4.leg0, Bauteil1.VIN
  N1: S3.leg1, R4.Pin_1
  N2: S4.leg1, R3.Pin_0
  N3: Bauteil1.5V, R1.Pin_1, R2.Pin_1
  N4: Bauteil1.D8, U1.Pin_4
  N5: Bauteil1.D7, U2.Pin_4
  N6: U1.Pin_1, R3.Pin_1
  N7: U1.Pin_2, LED1.A
  N8: U1.Pin_5, R1.Pin_0
  N9: U2.Pin_1, R4.Pin_0
  N10: U2.Pin_2, LED2.A
  N11: U2.Pin_5, R2.Pin_0
