# Fritzing sketch Fhotibot2 (saved by Fritzing 0.7.0b)
breadboards: 1

parts:
  Arduino1 = Arduino
  J1 = Infrared Proximity Sensor
  S2 = Pushbutton [package="[THT]"]
  Bauteil1 = SRF05 Ultrasonic Rangefinder
  LED1 = LED - 5mm [color="Red (633nm)" package="5 mm [THT]"]  # not connected
  R1 = Resistor [tolerance=±5% resistance=220 package=THT]

nets:
  N1: Arduino1.D8, S2.Pin_2, R1.Pin_0
  VCC: Arduino1.+5V, J1.Vcc, S2.Pin_3, S2.Pin_4, Bauteil1.VCC
  GND: Arduino1.GND, J1.GND, Bauteil1.GND, R1.Pin_1
  N2: Arduino1.A0, J1.Vout
  N3: Arduino1.A4, Bauteil1.Trig
  N4: Arduino1.A5, Bauteil1.Echo
