# Fritzing sketch SpaghuzzinatorElectronics (saved by Fritzing 0.7.1b)
breadboards: 1

parts:
  Arduino1 = Arduino
  J1 = Basic Servo
  C1 = Electrolytic Capacitor [capacitance=0.47mF voltage=16V package="200 mil [THT, electrolytic]"]
  R4 = Resistor [tolerance=±5% resistance=220 package=THT]

nets:
  GND: Arduino1.GND, J1.gnd, C1.-
  N1: Arduino1.D9, R4.Pin_1
  +5V: Arduino1.+5V, J1.vcc, C1.+
  N2: J1.pulse, R4.Pin_0
