# Fritzing sketch AstronautBackpack (saved by Fritzing 0.9.2b)
breadboards: 1

parts:
  Raspberry_Pi_B_rev1 = Raspberry Pi B rev1
  U1 = Battery Holders [package=battcon_20mm]
  R1 = Resistor [tolerance=±5% resistance=10k package="0603 [SMD]"]
  S1 = Pushbutton [package="[SMD]"]
  S2 = Pushbutton [package="[SMD]"]
  R6 = Resistor [tolerance=±5% resistance=10k package="0603 [SMD]"]
  S3 = Pushbutton [package="[SMD]"]
  R7 = Resistor [tolerance=±5% resistance=10k package="0603 [SMD]"]
  S4 = Pushbutton [package="[SMD]"]
  R8 = Resistor [tolerance=±5% resistance=10k package="0603 [SMD]"]
  S5 = Pushbutton [package="[SMD]"]
  R9 = Resistor [tolerance=±5% resistance=10k package="0603 [SMD]"]
  R10 = Resistor [tolerance=±5% resistance=220 package=THT]
  LED1 = LEDs [package=led10mm]
  LED2 = LEDs [package=led10mm]
  R11 = Resistor [tolerance=±5% resistance=220 package=THT]
  LED3 = LEDs [package=led10mm]
  LED4 = LEDs [package=led10mm]
  U2 = SWITCH_SPDT [package=kps-1290]
  U3 = SWITCH_SPDT [package=kps-1290]
  SPKR1 = Loudspeaker

nets:
  N1: Raspberry_Pi_B_rev1.5V, U1.+, S1.Pin_1, S1.Pin_2, S2.Pin_1, S2.Pin_2, S3.Pin_1, S3.Pin_2, S4.Pin_1, S4.Pin_2, S5.Pin_1, S5.Pin_2, U2.O, U2.P, U3.O
  N2: Raspberry_Pi_B_rev1.GND, U1.-, R1.Pin_0, R6.Pin_0, R7.Pin_0, R8.Pin_0, R9.Pin_0, LED1.C, LED3.C, SPKR1.pin1
  N3: Raspberry_Pi_B_rev1.GPIO_17, R1.Pin_1, S1.Pin_3, S1.Pin_4
  N4: Raspberry_Pi_B_rev1.GPIO_18, S2.Pin_3, S2.Pin_4, R6.Pin_1
  N5: Raspberry_Pi_B_rev1.GPIO_21, S3.Pin_3, S3.Pin_4, R7.Pin_1
  N6: Raspberry_Pi_B_rev1.GPIO_22, S4.Pin_3, S4.Pin_4, R8.Pin_1
  N7: Raspberry_Pi_B_rev1.GPIO_10, S5.Pin_3, S5.Pin_4, R9.Pin_1
  N8: R10.Pin_0, R11.Pin_0, U3.P
  N9: R10.Pin_1, LED1.A, LED2.A
  N10: R11.Pin_1, LED3.A, LED4.A
